# Fritzing sketch layout (saved by Fritzing 0.9.2b)
breadboards: 1

parts:
  Part1 = SparkFun ESP8266 Thing  # not connected
  R1 = Resistor [tolerance=±5% resistance=10k package=THT]
  R2 = Resistor [tolerance=±5% resistance=220k package=THT]
  R3 = Resistor [tolerance=±5% resistance=100k package=THT]
  R4 = Photocell (LDR) [package=THT]

nets:
  N1: R1.Pin_0, R2.Pin_0, R4.pin_0
  N2: R2.Pin_1, R3.Pin_0

notes:
  A voltage divider consists of a 220k and a 100k ohm resistor to scale 0 - 3.3V to 0 - 1V
